// Logisim project cpu.circ as structural Verilog: 1 circuit, main circuit main
module main (
  input  A,
  input  in_2,
  input  C,
  output out_4,
  output out_5
);

  wire and_1_out, and_2_out, and_3_out, clock_1_out, d_ff_1_q, xor_1_out;

  Clock clock_1 (.out(clock_1_out));
  xor xor_1 (xor_1_out, A, in_2);
  and and_1 (and_1_out, A, in_2);
  and and_2 (and_2_out, A, C);
  and and_3 (and_3_out, in_2, C);
  xor XOR2 (out_4, xor_1_out, C);
  or or_1 (out_5, and_1_out, and_2_out, and_3_out);
  D_Flip_Flop d_ff_1 (.D(out_5), .clk(clock_1_out), .Q(d_ff_1_q));  // open: Qn, preset, reset
  // Shift_Register #(.length(16), .parallel("false")) shift_register_1: pin names not known; wires that end beside it: clock_1_out, out_4
endmodule
